# Fritzing sketch LDR_module (saved by Fritzing 0.9.3b)

parts:
  KY-1 = Keyes Photo Resistor Sensor [package=THT]
  Part1 = Arduino Uno (Rev3)

nets:
  N1: KY-1.signal, Part1.A0
  N2: KY-1.power, Part1.5V
  N3: KY-1.ground, Part1.GND

custom parts:
  Keyes Photo Resistor Sensor: Keyes Photo Resistor Sensor Module for Arduino.

// code stored in the sketch: LDR_module.ino

#define LDR_PIN A0 

unsigned int LDR_value; 
void setup()
{
Serial.begin(9600); 
}

void loop()
{
LDR_value = analogRead(LDR_PIN); 
Serial.print("Light Voltage: "); 
Serial.println(LDR_value); 
delay(500); 
}
