# Fritzing sketch LDR_module2 (saved by Fritzing 0.9.3b)

parts:
  Part1 = Arduino Uno (Rev3)  # not connected
  Part2 = Arduino Sensor Shield v5.0
  KY-1 = Keyes Photo Resistor Sensor [package=THT]
  LED1 = LED - 3W Aluminum PCB  # not connected
  Part3 = KY-011 Two Color LED Module [package="Breakout board"]
  Part4 = KY-006 Passive Buzzer Module [package="Breakout board"]

nets:
  N1: Part2.A0, KY-1.signal
  N2: Part2.+5V#35, Part2.+5V#104, Part2.+5V#105, Part3.Vin
  N3: Part2.GND#53, Part2.GND#119, Part2.GND#120, Part3.-, Part4.-
  N4: Part2.D11, Part3.S
  N5: Part2.D12, Part4.S
  N6: Part2.GND#132, KY-1.ground
  N7: Part2.+5V#138, KY-1.power

custom parts:
  Keyes Photo Resistor Sensor: Keyes Photo Resistor Sensor Module for Arduino.
  LED - 3W Aluminum PCB: Description: So much power and light from such a small package. This 5 pack of red 3 Watt aluminum backed PCBs is sure to shed a lot of light on any project you add it to. These LEDs act as any other LED except these little guys require much more power while delivering a light as intense of a thousand suns going super nova (this is an exaggeration but you know what we mean)! Each LED in the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
  KY-011 Two Color LED Module: KEYES KY-011 Two Color LED Module consist of a common cathode 3mm red/green LED.
  KY-006 Passive Buzzer Module: Passive Piezoelectric Buzzer Module Keyes KY-006, it can produce a range of sound tones depending on the input frequency.
